# Fritzing sketch piedinatura_mattonella (saved by Fritzing 0.9.2b)
circuit board: 8.46667cm x 5.64444cm

parts:
  J1 = shrouded pin header, 16 pins [form="♂ (shrouded male)"]
  Part1 = Arduino Nano (Rev3.0)

nets:
  N1: J1.pin1, Part1.D2
  N2: J1.pin2, Part1.D4
  N3: J1.pin3, Part1.D5
  N4: J1.pin4, Part1.D7
  N5: J1.pin5, Part1.A0
  N6: J1.pin6, Part1.A2
  N7: J1.pin7, Part1.D8
  N8: J1.pin8, Part1.D9
  N9: J1.pin10, Part1.A4
  N10: J1.pin11, Part1.A3
  N11: J1.pin12, Part1.A1
  N12: J1.pin14, Part1.D6
  N13: J1.pin15, Part1.GND
  N14: J1.pin16, Part1.D3

notes:
  1
  15
  16
  30
